// Logisim project stack.circ as structural Verilog: 1 circuit, main circuit Stack
module Stack (
  input  [7:0] Din,
  input  CLK,
  input  pop,
  input  push,
  output [7:0] Dout,
  output empty,
  output full
);

  wire and_1_out, and_2_out, enable, nor_1_out, xor_1_out;
  wire [7:0] S_2_q;
  wire [8:0] multiplexer_1_out, multiplexer_2_out, multiplexer_3_out, S_1_q;
  wire [8:8] S_0_q;

  and and_1 (and_1_out, push, full);
  and and_2 (and_2_out, pop, empty);
  nor nor_1 (nor_1_out, and_1_out, and_2_out);
  xor xor_1 (xor_1_out, pop, push);
  and and_3 (enable, nor_1_out, xor_1_out);
  Multiplexer #(.width(9), .enable("false")) multiplexer_1 (
    .in0({S_0_q[8], Dout}), .in1({full, S_2_q}), .out(multiplexer_1_out), .sel(pop));
  Multiplexer #(.width(9), .enable("false")) multiplexer_2 (
    .in0(S_1_q), .in1({9{1'b0}}), .out(multiplexer_2_out), .sel(pop));
  Multiplexer #(.width(9), .enable("false")) multiplexer_3 (
    .in0({1'b1, Din}), .in1(S_1_q), .out(multiplexer_3_out), .sel(pop));
  Register #(.width(9)) S_0 (.D(multiplexer_3_out), .en(enable), .Q({S_0_q[8], Dout}), .clk(CLK));  // open: clr
  Register #(.width(9)) S_1 (.D(multiplexer_1_out), .en(enable), .Q(S_1_q), .clk(CLK));  // open: clr
  Register #(.width(9)) S_2 (.D(multiplexer_2_out), .en(enable), .Q({full, S_2_q}), .clk(CLK));  // open: clr
  not not_1 (empty, S_0_q[8]);
endmodule
